# Fritzing sketch seed-XIAO-RP2040-Blinking (saved by Fritzing 0.9.10b)
breadboards: 1

parts:
  S1 = Pushbutton [package="[THT]"]
  A1 = seeeduino-xiao

nets:
  N1: S1.Pin_1, S1.Pin_2, A1.GND
  N2: S1.Pin_3, S1.Pin_4, A1.D0

custom parts:
  seeeduino-xiao: Seeeduino XIAO processor board SMD version.
